// Logisim project makp2.circ as structural Verilog: 1 circuit, main circuit main
module main (
  input  in_1,
  input  in_2,
  input  in_3
);

  wire ALUSrc, and_1_out, and_2_out, and_3_out, and_4_out, and_5_out, and_7_out, and_13_out, and_14_out,
       and_15_out, and_16_out, and_17_out, and_18_out, and_19_out, and_20_out, and_21_out, and_22_out,
       and_23_out, and_24_out, and_25_out, and_26_out, and_27_out, and_28_out, and_29_out, and_30_out,
       and_31_out, auipc, Branch, CLK, clock_1_out, comparator_1_eq, comparator_1_gt, comparator_1_lt,
       comparator_2_eq, comparator_2_gt, comparator_2_lt, controlled_buffer_1_out, CSRSrc, CSRWE,
       demultiplexer_2_out0, demultiplexer_2_out1, demultiplexer_2_out2, demultiplexer_2_out4,
       demultiplexer_2_out5, demultiplexer_3_out0, demultiplexer_3_out4, demultiplexer_4_out0,
       demultiplexer_4_out1, demultiplexer_4_out2, demultiplexer_5_out0, demultiplexer_5_out1,
       demultiplexer_5_out2, demultiplexer_5_out3, demultiplexer_6_out0, demultiplexer_6_out1,
       demultiplexer_6_out2, demultiplexer_6_out3, demultiplexer_7_out1, demultiplexer_7_out2,
       demultiplexer_7_out3, demultiplexer_7_out4, demultiplexer_7_out5, demultiplexer_7_out6,
       demultiplexer_7_out7, demultiplexer_7_out8, demultiplexer_7_out9, demultiplexer_7_out10,
       demultiplexer_7_out11, demultiplexer_7_out12, demultiplexer_7_out13, demultiplexer_7_out14,
       demultiplexer_7_out15, demultiplexer_7_out16, demultiplexer_7_out17, demultiplexer_7_out18,
       demultiplexer_7_out19, demultiplexer_7_out20, demultiplexer_7_out21, demultiplexer_7_out22,
       demultiplexer_7_out23, demultiplexer_7_out24, demultiplexer_7_out25, demultiplexer_7_out26,
       demultiplexer_7_out27, demultiplexer_7_out28, demultiplexer_7_out29, demultiplexer_7_out30,
       demultiplexer_7_out31, ecall, Env, jalr, Jump, keyboard_1_avail, lui, MemRead, MemWrite, mret,
       nor_1_out, not_1_out, not_2_out, not_3_out, not_5_out, not_6_out, not_7_out, not_8_out, not_9_out,
       not_10_out, not_11_out, not_12_out, not_13_out, not_14_out, not_15_out, or_1_out, or_2_out, or_3_out,
       or_5_out, or_7_out, or_8_out, or_9_out, or_10_out, or_11_out, or_12_out, or_13_out, or_14_out,
       or_15_out, or_16_out, or_18_out, or_19_out, priv_mode, priv_q, RegWrite, system, trap;
  wire [1:0] ALUOp, controlled_buffer_3_out, controlled_buffer_21_out, CSRWMode, demultiplexer_1_out0,
       multiplexer_8_out, multiplexer_9_out;
  wire [2:0] f3, ImmSel;
  wire [3:0] ALUControl, rom_2_data, rom_3_data;
  wire [4:0] multiplexer_33_out, rd, rs1, rs2;
  wire [6:0] bit_extender_1_out, f7, keyboard_1_data, multiplexer_1_out;
  wire [7:0] multiplexer_14_out, multiplexer_15_out, multiplexer_16_out, multiplexer_17_out,
       multiplexer_27_out, multiplexer_28_out, multiplexer_29_out, multiplexer_30_out, ram_1_dout,
       ram_2_dout, ram_3_dout, ram_4_dout;
  wire [11:0] CSRAddr, xnor_1_out, xnor_2_out, xnor_3_out, xnor_4_out, xnor_5_out, xnor_6_out, xnor_7_out;
  wire [21:0] adder_2_out, bit_extender_2_out, demultiplexer_1_out0_2, multiplexer_18_out,
       multiplexer_19_out, multiplexer_20_out;
  wire [23:0] adder_1_out, demultiplexer_1_out1, multiplexer_3_out, multiplexer_4_out, PC, PCNext,
       subtractor_1_out;
  wire [24:0] multiplexer_7_out;
  wire [31:0] adder_3_out, ALUOut, and_32_out, and_33_out, bit_extender_3_out, bit_extender_4_out,
       bit_extender_5_out, bit_extender_6_out, bit_extender_7_out, bit_extender_8_out, bit_extender_9_out,
       bit_extender_10_out, bit_extender_11_out, bit_extender_12_out, bit_extender_13_out,
       bit_extender_14_out, bit_extender_15_out, bit_extender_16_out, bit_extender_17_out,
       bit_extender_18_out, bit_extender_19_out, controlled_buffer_17_out, controlled_buffer_19_out, CSRLU,
       CSROut, Imm, IR, mcause_q, mcauseD, mepc, mepcD, mscratch_q, mstatus, mstatusD, mtvec,
       multiplexer_22_out, multiplexer_23_out, multiplexer_24_out, multiplexer_32_out, multiplexer_34_out,
       or_17_out, or_20_out, RAMOut, reg1, reg2, shifter_1_out, shifter_2_out, shifter_3_out,
       subtractor_3_out, trapCause, x1_q, x2_q, x3_q, x4_q, x5_q, x6_q, x7_q, x8_q, x9_q, x10_q, x11_q,
       x12_q, x13_q, x14_q, x15_q, x16_q, x17_q, x18_q, x19_q, x20_q, x21_q, x22_q, x23_q, x24_q, x25_q,
       x26_q, x27_q, x28_q, x29_q, x30_q, x31_q, xor_1_out;

  not not_1 (not_1_out, mstatus[11]);
  assign controlled_buffer_1_out = trap ? 1'b0 : 1'bz;  // Controlled_Buffer controlled_buffer_1
  assign controlled_buffer_1_out = mret ? not_1_out : 1'bz;  // Controlled_Buffer controlled_buffer_2
  and and_1 (and_1_out, Branch, ALUOut[0]);
  or or_1 (or_1_out, and_1_out, Jump);
  assign controlled_buffer_3_out = trap ? 2'b10 : 2'bz;  // Controlled_Buffer controlled_buffer_3
  assign controlled_buffer_3_out = jalr ? 2'b01 : 2'bz;  // Controlled_Buffer controlled_buffer_4
  Clock clock_1 (.out(clock_1_out));
  Register #(.width(1)) priv (.D(controlled_buffer_1_out), .en(or_2_out), .clk(not_2_out), .Q(priv_q));  // open: clr
  or or_2 (or_2_out, mret, trap);
  not not_2 (not_2_out, CLK);
  and and_2 (and_2_out, not_5_out, not_7_out);
  Subtractor #(.width(24)) subtractor_1 (.a(Imm[23:0]), .b(24'h4), .out(subtractor_1_out));  // open: bin, bout
  assign controlled_buffer_3_out = mret ? 2'b11 : 2'bz;  // Controlled_Buffer controlled_buffer_5
  assign controlled_buffer_3_out = and_3_out ? 2'b00 : 2'bz;  // Controlled_Buffer controlled_buffer_6
  and and_3 (and_3_out, ~mret, ~trap, ~jalr);  // AND_Gate
  or or_3 (or_3_out, mret, or_1_out, trap, jalr);
  not not_3 (not_3_out, CLK);
  Multiplexer #(.width(32)) multiplexer_1 (
    .in0(32'h33), .in1(IR), .out({f7, rs2, rs1, f3, rd, multiplexer_1_out}), .sel(CLK));
  not not_4 (priv_mode, priv_q);
  buf or_4 (trap, ecall);  // OR_Gate
  assign trapCause = and_4_out ? 32'h8 : 32'bz;  // Controlled_Buffer controlled_buffer_7
  not not_5 (not_5_out, and_4_out);
  and and_4 (and_4_out, ecall, not_6_out);
  not not_6 (not_6_out, priv_mode);
  assign trapCause = and_5_out ? 32'hb : 32'bz;  // Controlled_Buffer controlled_buffer_8
  not not_7 (not_7_out, and_5_out);
  and and_5 (and_5_out, ecall, priv_mode);
  and and_6 (CLK, in_3, clock_1_out);
  ROM #(.addrWidth(5), .dataWidth(11)) rom_1 (
    .addr(multiplexer_1_out[6:2]), .data({ImmSel, ALUOp, Jump, Branch, MemWrite, MemRead, ALUSrc, RegWrite}));
  Multiplexer #(.width(3)) multiplexer_2 (.in0(3'b100), .in1(f3), .out({CSRSrc, CSRWMode}), .sel(system));
  assign CSRAddr = system ? {f7, rs2} : 12'bz;  // Controlled_Buffer controlled_buffer_9
  assign trapCause = and_2_out ? {32{1'b0}} : 32'bz;  // Controlled_Buffer controlled_buffer_10
  Multiplexer #(.select(2), .width(24)) multiplexer_3 (
    .in0(adder_1_out), .in1(ALUOut[23:0]), .in2(mtvec[23:0]), .in3(mepc[23:0]), .out(multiplexer_3_out),
    .sel(controlled_buffer_3_out));
  or or_5 (or_5_out, CLK, and_7_out);
  and and_7 (and_7_out, or_3_out, not_3_out);
  and and_8 (auipc, ~multiplexer_1_out[6], ~multiplexer_1_out[5], multiplexer_1_out[4], ~multiplexer_1_out[3], multiplexer_1_out[2]);  // AND_Gate
  and and_9 (lui, ~multiplexer_1_out[6], multiplexer_1_out[5], multiplexer_1_out[4], ~multiplexer_1_out[3], multiplexer_1_out[2]);  // AND_Gate
  and and_10 (jalr, multiplexer_1_out[6], multiplexer_1_out[5], ~multiplexer_1_out[4], ~multiplexer_1_out[3], multiplexer_1_out[2]);  // AND_Gate
  and and_11 (system, multiplexer_1_out[6], multiplexer_1_out[5], multiplexer_1_out[4], ~multiplexer_1_out[3], ~multiplexer_1_out[2]);  // AND_Gate
  and and_12 (Env, ~CSRWMode[0], ~CSRWMode[1], ~CSRSrc);  // AND_Gate
  or or_6 (CSRWE, CSRWMode[0], CSRWMode[1]);
  Multiplexer #(.width(24)) multiplexer_4 (
    .in0(24'h4), .in1(subtractor_1_out), .out(multiplexer_4_out), .sel(or_1_out));
  Register #(.width(24)) register_1 (.D(multiplexer_3_out), .clk(or_5_out), .Q(PCNext), .clr(in_1));  // open: en
  and and_13 (and_13_out, system, Env);
  assign xnor_1_out = ~({f7, rs2} ^ {12{1'b0}});  // XNOR_Gate xnor_1, 12 bits wide
  and and_14 (and_14_out, xnor_1_out[0], xnor_1_out[1], xnor_1_out[2], xnor_1_out[3], xnor_1_out[4], xnor_1_out[5], xnor_1_out[6], xnor_1_out[7], xnor_1_out[8], xnor_1_out[9], xnor_1_out[10], xnor_1_out[11]);
  assign xnor_2_out = ~({f7, rs2} ^ 12'h302);  // XNOR_Gate xnor_2, 12 bits wide
  and and_15 (and_15_out, xnor_2_out[0], xnor_2_out[1], xnor_2_out[2], xnor_2_out[3], xnor_2_out[4], xnor_2_out[5], xnor_2_out[6], xnor_2_out[7], xnor_2_out[8], xnor_2_out[9], xnor_2_out[10], xnor_2_out[11]);
  Adder #(.width(24)) adder_1 (.a(multiplexer_4_out), .b(PCNext), .out(adder_1_out));  // open: cin, cout
  Subtractor #(.width(24)) subtractor_2 (.a(PCNext), .b(24'h4), .out(PC));  // open: bin, bout
  Multiplexer multiplexer_5 (.in0(1'b0), .in1(and_14_out), .out(ecall), .sel(and_13_out));
  Multiplexer multiplexer_6 (.in0(1'b0), .in1(and_15_out), .out(mret), .sel(and_13_out));
  or or_7 (or_7_out, MemRead, MemWrite);
  Multiplexer #(.width(25)) multiplexer_7 (
    .in0({1'b0, PCNext}), .in1(ALUOut[24:0]), .out(multiplexer_7_out), .sel(or_7_out));
  not not_8 (not_8_out, multiplexer_7_out[24]);
  and and_16 (and_16_out, not_8_out, MemWrite);
  and and_17 (and_17_out, MemWrite, multiplexer_7_out[24]);
  Demultiplexer #(.width(24)) demultiplexer_1 (
    .out0({demultiplexer_1_out0_2, demultiplexer_1_out0}), .out1(demultiplexer_1_out1),
    .in(multiplexer_7_out[23:0]), .sel(multiplexer_7_out[24]));
  Multiplexer #(.width(2)) multiplexer_8 (.in0(2'b10), .in1(f3[1:0]), .out(multiplexer_8_out), .sel(MemWrite));
  Multiplexer #(.width(2)) multiplexer_9 (.in0(2'b00), .in1({f7[5], f7[0]}), .out(multiplexer_9_out), .sel(or_8_out));
  or or_8 (or_8_out, and_19_out, not_10_out);
  not not_9 (not_9_out, CLK);
  Demultiplexer #(.select(3)) demultiplexer_2 (
    .out0(demultiplexer_2_out0), .out1(demultiplexer_2_out1), .out2(demultiplexer_2_out2),
    .out4(demultiplexer_2_out4), .out5(demultiplexer_2_out5), .in(not_9_out), .sel(demultiplexer_1_out1[4:2]));  // open: out3, out6, out7
  Demultiplexer #(.select(3)) demultiplexer_3 (
    .out0(demultiplexer_3_out0), .out4(demultiplexer_3_out4), .in(and_17_out), .sel(demultiplexer_1_out1[4:2]));  // open: out1, out2, out3, out5, out6, out7
  Demultiplexer #(.select(2)) demultiplexer_4 (
    .out0(demultiplexer_4_out0), .out1(demultiplexer_4_out1), .out2(demultiplexer_4_out2), .in(and_16_out),
    .sel(multiplexer_8_out));  // open: out3
  and and_18 (and_18_out, ~ALUOp[0], ALUOp[1]);  // AND_Gate
  not not_10 (not_10_out, and_18_out);
  Multiplexer #(.select(2), .width(32)) multiplexer_10 (
    .in0(CSRLU),
    .in1({mstatus[31:13], {2{priv_mode}}, mstatus[10:8], mstatus[3], mstatus[6:4], 1'b0, mstatus[2:0]}),
    .in2({mstatus[31:4], mstatus[7], mstatus[2:0]}), .out(mstatusD), .sel({mret, trap}));  // open: in3
  Multiplexer #(.width(32)) multiplexer_11 (.in0(CSRLU), .in1({{8{1'b0}}, PC}), .out(mepcD), .sel(trap));
  Multiplexer #(.width(32)) multiplexer_12 (.in0(CSRLU), .in1(trapCause), .out(mcauseD), .sel(trap));
  Bit_Extender #(.in_width(32), .out_width(7)) bit_extender_1 (.in(reg2), .out(bit_extender_1_out));
  TTY #(.cols(38), .rows(16)) tty_1 (
    .data(bit_extender_1_out), .clk(demultiplexer_2_out0), .we(demultiplexer_3_out0),
    .clr(demultiplexer_2_out1));
  Demultiplexer #(.select(2)) demultiplexer_5 (
    .out0(demultiplexer_5_out0), .out1(demultiplexer_5_out1), .out2(demultiplexer_5_out2),
    .out3(demultiplexer_5_out3), .in(demultiplexer_4_out1), .sel(demultiplexer_1_out0));
  Demultiplexer #(.select(2)) demultiplexer_6 (
    .out0(demultiplexer_6_out0), .out1(demultiplexer_6_out1), .out2(demultiplexer_6_out2),
    .out3(demultiplexer_6_out3), .in(demultiplexer_4_out0), .sel(demultiplexer_1_out0));
  and and_19 (and_19_out, and_18_out, or_9_out);
  or or_9 (or_9_out, and_20_out, and_21_out);
  and and_20 (and_20_out, f3[0], ~f3[1], f3[2]);  // AND_Gate
  and and_21 (and_21_out, f3[0], ~f3[1], ~f3[2]);  // AND_Gate
  Bit_Extender #(.in_width(32), .out_width(22)) bit_extender_2 (.in(reg2), .out(bit_extender_2_out));
  Adder #(.width(22)) adder_2 (.a(demultiplexer_1_out0_2), .b(22'h1), .out(adder_2_out));  // open: cin, cout
  assign bit_extender_3_out = {{20{f7[6]}}, {f7, rs2}};  // Bit_Extender bit_extender_3
  assign bit_extender_4_out = {{20{f7[6]}}, {f7, rd}};  // Bit_Extender bit_extender_4
  assign bit_extender_5_out = {{19{f7[6]}}, {f7[6], rd[0], f7[5:0], rd[4:1], 1'b0}};  // Bit_Extender bit_extender_5
  assign bit_extender_6_out = {{11{f7[6]}}, {f7[6], rs1, f3, rs2[0], f7[5:0], rs2[4:1], 1'b0}};  // Bit_Extender bit_extender_6
  ROM #(.addrWidth(5), .dataWidth(4)) rom_2 (.addr({multiplexer_9_out, f3}), .data(rom_2_data));
  ROM #(.addrWidth(3), .dataWidth(4)) rom_3 (.addr(f3), .data(rom_3_data));
  assign xnor_3_out = ~(CSRAddr ^ 12'h300);  // XNOR_Gate xnor_3, 12 bits wide
  assign xnor_4_out = ~(CSRAddr ^ 12'h341);  // XNOR_Gate xnor_4, 12 bits wide
  assign xnor_5_out = ~(CSRAddr ^ 12'h342);  // XNOR_Gate xnor_5, 12 bits wide
  assign xnor_6_out = ~(CSRAddr ^ 12'h305);  // XNOR_Gate xnor_6, 12 bits wide
  assign xnor_7_out = ~(CSRAddr ^ 12'h340);  // XNOR_Gate xnor_7, 12 bits wide
  // RGB_Video #(.cursor("No Cursor")) rgb_video_1: pin names not known; wires that end beside it: demultiplexer_2_out5, demultiplexer_2_out4, demultiplexer_3_out4, bit_extender_2_out[6:0], bit_extender_2_out[13:7], bit_extender_2_out[21:14]
  Multiplexer #(.select(3), .width(32)) multiplexer_13 (
    .in0(bit_extender_3_out), .in1(bit_extender_4_out), .in2(bit_extender_5_out),
    .in3({f7, rs2, rs1, f3, {12{1'b0}}}), .in4(bit_extender_6_out), .out(Imm), .sel(ImmSel));  // open: in5, in6, in7
  and and_22 (and_22_out, xnor_3_out[0], xnor_3_out[1], xnor_3_out[2], xnor_3_out[3], xnor_3_out[4], xnor_3_out[5], xnor_3_out[6], xnor_3_out[7], xnor_3_out[8], xnor_3_out[9], xnor_3_out[10], xnor_3_out[11]);
  and and_23 (and_23_out, xnor_4_out[0], xnor_4_out[1], xnor_4_out[2], xnor_4_out[3], xnor_4_out[4], xnor_4_out[5], xnor_4_out[6], xnor_4_out[7], xnor_4_out[8], xnor_4_out[9], xnor_4_out[10], xnor_4_out[11]);
  and and_24 (and_24_out, xnor_5_out[0], xnor_5_out[1], xnor_5_out[2], xnor_5_out[3], xnor_5_out[4], xnor_5_out[5], xnor_5_out[6], xnor_5_out[7], xnor_5_out[8], xnor_5_out[9], xnor_5_out[10], xnor_5_out[11]);
  and and_25 (and_25_out, xnor_6_out[0], xnor_6_out[1], xnor_6_out[2], xnor_6_out[3], xnor_6_out[4], xnor_6_out[5], xnor_6_out[6], xnor_6_out[7], xnor_6_out[8], xnor_6_out[9], xnor_6_out[10], xnor_6_out[11]);
  and and_26 (and_26_out, xnor_7_out[0], xnor_7_out[1], xnor_7_out[2], xnor_7_out[3], xnor_7_out[4], xnor_7_out[5], xnor_7_out[6], xnor_7_out[7], xnor_7_out[8], xnor_7_out[9], xnor_7_out[10], xnor_7_out[11]);
  Keyboard keyboard_1 (.clk(demultiplexer_2_out2), .avail(keyboard_1_avail), .data(keyboard_1_data));  // open: re, clr
  Multiplexer #(.select(2), .width(8)) multiplexer_14 (
    .in0(reg2[7:0]), .in1(reg2[31:24]), .in2(reg2[23:16]), .in3(reg2[15:8]), .out(multiplexer_14_out),
    .sel(demultiplexer_1_out0));
  Multiplexer #(.select(2), .width(8)) multiplexer_15 (
    .in0(reg2[15:8]), .in1(reg2[7:0]), .in2(reg2[31:24]), .in3(reg2[23:16]), .out(multiplexer_15_out),
    .sel(demultiplexer_1_out0));
  Multiplexer #(.select(2), .width(8)) multiplexer_16 (
    .in0(reg2[23:16]), .in1(reg2[15:8]), .in2(reg2[7:0]), .in3(reg2[31:24]), .out(multiplexer_16_out),
    .sel(demultiplexer_1_out0));
  Multiplexer #(.select(2), .width(8)) multiplexer_17 (
    .in0(reg2[31:24]), .in1(reg2[23:16]), .in2(reg2[15:8]), .in3(reg2[7:0]), .out(multiplexer_17_out),
    .sel(demultiplexer_1_out0));
  Register #(.width(32)) u_mstatus (.D(mstatusD), .en(or_10_out), .clk(not_11_out), .Q(mstatus));  // open: clr
  or or_10 (or_10_out, trap, mret, and_27_out);
  and and_27 (and_27_out, and_22_out, CSRWE, priv_mode);
  not not_11 (not_11_out, CLK);
  Register #(.width(32)) u_mepc (.D(mepcD), .en(or_11_out), .clk(not_11_out), .Q(mepc));  // open: clr
  or or_11 (or_11_out, trap, and_28_out);
  and and_28 (and_28_out, and_23_out, CSRWE, priv_mode);
  Register #(.width(32)) mcause (.D(mcauseD), .en(or_12_out), .clk(not_11_out), .Q(mcause_q));  // open: clr
  or or_12 (or_12_out, trap, and_29_out);
  and and_29 (and_29_out, and_24_out, CSRWE, priv_mode);
  Register #(.width(32)) u_mtvec (.D(CSRLU), .en(and_30_out), .clk(not_11_out), .Q(mtvec));  // open: clr
  and and_30 (and_30_out, CSRWE, and_25_out, priv_mode);
  Register #(.width(32)) mscratch (.D(CSRLU), .en(and_31_out), .clk(not_11_out), .Q(mscratch_q));  // open: clr
  and and_31 (and_31_out, CSRWE, and_26_out, priv_mode);
  Multiplexer #(.select(2), .width(22)) multiplexer_18 (
    .in0(demultiplexer_1_out0_2), .in1(adder_2_out), .in2(adder_2_out), .in3(adder_2_out),
    .out(multiplexer_18_out), .sel(demultiplexer_1_out0));
  Multiplexer #(.select(2), .width(22)) multiplexer_19 (
    .in0(demultiplexer_1_out0_2), .in1(demultiplexer_1_out0_2), .in2(adder_2_out), .in3(adder_2_out),
    .out(multiplexer_19_out), .sel(demultiplexer_1_out0));
  Multiplexer #(.select(2), .width(22)) multiplexer_20 (
    .in0(demultiplexer_1_out0_2), .in1(demultiplexer_1_out0_2), .in2(demultiplexer_1_out0_2),
    .in3(adder_2_out), .out(multiplexer_20_out), .sel(demultiplexer_1_out0));
  assign CSROut = and_22_out ? mstatus : 32'bz;  // Controlled_Buffer controlled_buffer_11
  assign CSROut = and_23_out ? mepc : 32'bz;  // Controlled_Buffer controlled_buffer_12
  assign CSROut = and_24_out ? mcause_q : 32'bz;  // Controlled_Buffer controlled_buffer_13
  assign CSROut = and_25_out ? mtvec : 32'bz;  // Controlled_Buffer controlled_buffer_14
  assign CSROut = and_26_out ? mscratch_q : 32'bz;  // Controlled_Buffer controlled_buffer_15
  assign bit_extender_7_out = {{25{1'b0}}, keyboard_1_data};  // Bit_Extender bit_extender_7
  assign bit_extender_8_out = {{31{1'b0}}, keyboard_1_avail};  // Bit_Extender bit_extender_8
  Multiplexer #(.select(2), .width(4)) multiplexer_21 (
    .in0(4'b0000), .in1(rom_2_data), .in2(rom_2_data), .in3(rom_3_data), .out(ALUControl), .sel(ALUOp));
  or or_13 (or_13_out, demultiplexer_4_out2, demultiplexer_5_out0, demultiplexer_5_out3, demultiplexer_6_out0);
  or or_14 (or_14_out, demultiplexer_4_out2, demultiplexer_5_out0, demultiplexer_5_out1, demultiplexer_6_out1);
  or or_15 (or_15_out, demultiplexer_4_out2, demultiplexer_5_out1, demultiplexer_5_out2, demultiplexer_6_out2);
  or or_16 (or_16_out, demultiplexer_4_out2, demultiplexer_5_out2, demultiplexer_5_out3, demultiplexer_6_out3);
  Multiplexer #(.width(32)) multiplexer_22 (.in0(reg1), .in1({32{1'b0}}), .out(multiplexer_22_out), .sel(lui));
  Multiplexer #(.width(32)) multiplexer_23 (.in0(reg2), .in1(Imm), .out(multiplexer_23_out), .sel(ALUSrc));
  Multiplexer #(.select(3), .width(32)) multiplexer_24 (
    .in2(bit_extender_7_out), .in3(bit_extender_8_out), .out(multiplexer_24_out),
    .sel(demultiplexer_1_out1[4:2]));  // open: in0, in1, in4, in5, in6, in7
  RAM #(.addrWidth(22), .asyncread("true"), .trigger("falling")) ram_1 (
    .addr(multiplexer_18_out), .we(or_13_out), .oe(1'b1), .clk(CLK), .din(multiplexer_14_out),
    .dout(ram_1_dout));
  RAM #(.addrWidth(22), .asyncread("true"), .trigger("falling")) ram_2 (
    .addr(multiplexer_19_out), .we(or_14_out), .oe(1'b1), .clk(CLK), .din(multiplexer_15_out),
    .dout(ram_2_dout));
  RAM #(.addrWidth(22), .asyncread("true"), .trigger("falling")) ram_3 (
    .addr(multiplexer_20_out), .we(or_15_out), .oe(1'b1), .clk(CLK), .din(multiplexer_16_out),
    .dout(ram_3_dout));
  RAM #(.addrWidth(22), .asyncread("true"), .trigger("falling")) ram_4 (
    .addr(demultiplexer_1_out0_2), .we(or_16_out), .oe(1'b1), .clk(CLK), .din(multiplexer_17_out),
    .dout(ram_4_dout));
  assign multiplexer_22_out = auipc ? {{8{1'b0}}, PC} : 32'bz;  // Controlled_Buffer controlled_buffer_16
  assign controlled_buffer_17_out = not_12_out ? reg1 : 32'bz;  // Controlled_Buffer controlled_buffer_17
  not not_12 (not_12_out, CSRSrc);
  assign bit_extender_9_out = {{27{1'b0}}, rs1};  // Bit_Extender bit_extender_9
  assign controlled_buffer_17_out = CSRSrc ? bit_extender_9_out : 32'bz;  // Controlled_Buffer controlled_buffer_18
  assign controlled_buffer_19_out = multiplexer_7_out[24] ? multiplexer_24_out : 32'bz;  // Controlled_Buffer controlled_buffer_19
  Adder #(.width(32)) adder_3 (.a(multiplexer_22_out), .b(multiplexer_23_out), .out(adder_3_out));  // open: cin, cout
  Subtractor #(.width(32)) subtractor_3 (
    .a(multiplexer_22_out), .b(multiplexer_23_out), .out(subtractor_3_out));  // open: bin, bout
  assign and_32_out = multiplexer_22_out & multiplexer_23_out;  // AND_Gate and_32, 32 bits wide
  assign or_17_out = multiplexer_22_out | multiplexer_23_out;  // OR_Gate or_17, 32 bits wide
  assign xor_1_out = multiplexer_22_out ^ multiplexer_23_out;  // XOR_Gate xor_1, 32 bits wide
  Shifter #(.width(32)) shifter_1 (.in(multiplexer_22_out), .\dist (multiplexer_23_out[4:0]), .out(shifter_1_out));
  Shifter #(.shift("lr"), .width(32)) shifter_2 (
    .in(multiplexer_22_out), .\dist (multiplexer_23_out[4:0]), .out(shifter_2_out));
  Shifter #(.shift("ar"), .width(32)) shifter_3 (
    .in(multiplexer_22_out), .\dist (multiplexer_23_out[4:0]), .out(shifter_3_out));
  or or_18 (or_18_out, comparator_1_gt, comparator_1_eq);
  not not_13 (not_13_out, comparator_1_eq);
  Comparator #(.width(32)) comparator_1 (
    .a(multiplexer_22_out), .b(multiplexer_23_out), .gt(comparator_1_gt), .eq(comparator_1_eq),
    .lt(comparator_1_lt));
  or or_19 (or_19_out, comparator_2_gt, comparator_2_eq);
  Comparator #(.mode("unsigned"), .width(32)) comparator_2 (
    .a(multiplexer_22_out), .b(multiplexer_23_out), .gt(comparator_2_gt), .eq(comparator_2_eq),
    .lt(comparator_2_lt));
  assign or_20_out = CSROut | controlled_buffer_17_out;  // OR_Gate or_20, 32 bits wide
  assign and_33_out = CSROut & ~controlled_buffer_17_out;  // AND_Gate and_33, 32 bits wide
  assign bit_extender_10_out = {{31{1'b0}}, or_18_out};  // Bit_Extender bit_extender_10
  assign bit_extender_11_out = {{31{1'b0}}, not_13_out};  // Bit_Extender bit_extender_11
  assign bit_extender_12_out = {{31{1'b0}}, comparator_1_eq};  // Bit_Extender bit_extender_12
  assign bit_extender_13_out = {{31{1'b0}}, comparator_1_lt};  // Bit_Extender bit_extender_13
  assign bit_extender_14_out = {{31{1'b0}}, or_19_out};  // Bit_Extender bit_extender_14
  assign bit_extender_15_out = {{31{1'b0}}, comparator_2_lt};  // Bit_Extender bit_extender_15
  Multiplexer #(.select(2), .width(32)) multiplexer_25 (
    .in1(reg1), .in2(or_20_out), .in3(and_33_out), .out(CSRLU), .sel(CSRWMode));  // open: in0
  Multiplexer #(.select(4), .width(32)) multiplexer_26 (
    .in0(adder_3_out), .in1(subtractor_3_out), .in2(and_32_out), .in3(or_17_out), .in4(xor_1_out),
    .in5(shifter_1_out), .in6(shifter_2_out), .in7(shifter_3_out), .in8(bit_extender_12_out),
    .in9(bit_extender_11_out), .in10(bit_extender_10_out), .in11(bit_extender_14_out),
    .in12(bit_extender_13_out), .in13(bit_extender_15_out), .out(ALUOut), .sel(ALUControl));  // open: in14, in15
  Multiplexer #(.select(2), .width(8)) multiplexer_27 (
    .in0(ram_1_dout), .in1(ram_2_dout), .in2(ram_3_dout), .in3(ram_4_dout), .out(multiplexer_27_out),
    .sel(demultiplexer_1_out0));
  Multiplexer #(.select(2), .width(8)) multiplexer_28 (
    .in0(ram_2_dout), .in1(ram_3_dout), .in2(ram_4_dout), .in3(ram_1_dout), .out(multiplexer_28_out),
    .sel(demultiplexer_1_out0));
  Multiplexer #(.select(2), .width(8)) multiplexer_29 (
    .in0(ram_3_dout), .in1(ram_4_dout), .in2(ram_1_dout), .in3(ram_2_dout), .out(multiplexer_29_out),
    .sel(demultiplexer_1_out0));
  Multiplexer #(.select(2), .width(8)) multiplexer_30 (
    .in0(ram_4_dout), .in1(ram_1_dout), .in2(ram_2_dout), .in3(ram_3_dout), .out(multiplexer_30_out),
    .sel(demultiplexer_1_out0));
  Register #(.width(32)) register_2 (.D(controlled_buffer_19_out), .clk(CLK), .Q(IR), .clr(in_2));  // open: en
  assign bit_extender_16_out = {{24{controlled_buffer_19_out[7]}}, controlled_buffer_19_out[7:0]};  // Bit_Extender bit_extender_16
  assign bit_extender_17_out = {{16{controlled_buffer_19_out[15]}}, controlled_buffer_19_out[15:0]};  // Bit_Extender bit_extender_17
  assign bit_extender_18_out = {{24{1'b0}}, controlled_buffer_19_out[7:0]};  // Bit_Extender bit_extender_18
  assign bit_extender_19_out = {{16{1'b0}}, controlled_buffer_19_out[15:0]};  // Bit_Extender bit_extender_19
  Multiplexer #(.select(3), .width(32)) multiplexer_31 (
    .in0(bit_extender_16_out), .in1(bit_extender_17_out), .in2(controlled_buffer_19_out),
    .in4(bit_extender_18_out), .in5(bit_extender_19_out), .out(RAMOut), .sel(f3));  // open: in3, in6, in7
  assign controlled_buffer_19_out = not_8_out ? {multiplexer_30_out, multiplexer_29_out, multiplexer_28_out, multiplexer_27_out} : 32'bz;  // Controlled_Buffer controlled_buffer_20
  assign controlled_buffer_21_out = MemRead ? 2'b01 : 2'bz;  // Controlled_Buffer controlled_buffer_21
  assign controlled_buffer_21_out = Jump ? 2'b10 : 2'bz;  // Controlled_Buffer controlled_buffer_22
  assign controlled_buffer_21_out = system ? 2'b11 : 2'bz;  // Controlled_Buffer controlled_buffer_23
  Multiplexer #(.select(2), .width(32)) multiplexer_32 (
    .in0(ALUOut), .in1(RAMOut), .in2({{8{1'b0}}, PCNext}), .in3(CSROut), .out(multiplexer_32_out),
    .sel(controlled_buffer_21_out));
  assign controlled_buffer_21_out = nor_1_out ? 2'b00 : 2'bz;  // Controlled_Buffer controlled_buffer_24
  nor nor_1 (nor_1_out, MemRead, Jump, system);
  Demultiplexer #(.select(5)) demultiplexer_7 (
    .out1(demultiplexer_7_out1), .out2(demultiplexer_7_out2), .out3(demultiplexer_7_out3),
    .out4(demultiplexer_7_out4), .out5(demultiplexer_7_out5), .out6(demultiplexer_7_out6),
    .out7(demultiplexer_7_out7), .out8(demultiplexer_7_out8), .out9(demultiplexer_7_out9),
    .out10(demultiplexer_7_out10), .out11(demultiplexer_7_out11), .out12(demultiplexer_7_out12),
    .out13(demultiplexer_7_out13), .out14(demultiplexer_7_out14), .out15(demultiplexer_7_out15),
    .out16(demultiplexer_7_out16), .out17(demultiplexer_7_out17), .out18(demultiplexer_7_out18),
    .out19(demultiplexer_7_out19), .out20(demultiplexer_7_out20), .out21(demultiplexer_7_out21),
    .out22(demultiplexer_7_out22), .out23(demultiplexer_7_out23), .out24(demultiplexer_7_out24),
    .out25(demultiplexer_7_out25), .out26(demultiplexer_7_out26), .out27(demultiplexer_7_out27),
    .out28(demultiplexer_7_out28), .out29(demultiplexer_7_out29), .out30(demultiplexer_7_out30),
    .out31(demultiplexer_7_out31), .in(1'b1), .sel(multiplexer_33_out));  // open: out0
  Multiplexer #(.width(5)) multiplexer_33 (.in0({5{1'b0}}), .in1(rd), .out(multiplexer_33_out), .sel(RegWrite));
  not not_14 (not_14_out, CLK);
  Register #(.width(32)) x31 (
    .D(multiplexer_32_out), .en(demultiplexer_7_out31), .clk(not_14_out), .Q(x31_q));  // open: clr
  Register #(.width(32)) x30 (
    .D(multiplexer_32_out), .en(demultiplexer_7_out30), .clk(not_14_out), .Q(x30_q));  // open: clr
  Register #(.width(32)) x29 (
    .D(multiplexer_32_out), .en(demultiplexer_7_out29), .clk(not_14_out), .Q(x29_q));  // open: clr
  Register #(.width(32)) x28 (
    .D(multiplexer_32_out), .en(demultiplexer_7_out28), .clk(not_14_out), .Q(x28_q));  // open: clr
  Register #(.width(32)) x27 (
    .D(multiplexer_32_out), .en(demultiplexer_7_out27), .clk(not_14_out), .Q(x27_q));  // open: clr
  Register #(.width(32)) x26 (
    .D(multiplexer_32_out), .en(demultiplexer_7_out26), .clk(not_14_out), .Q(x26_q));  // open: clr
  Register #(.width(32)) x25 (
    .D(multiplexer_32_out), .en(demultiplexer_7_out25), .clk(not_14_out), .Q(x25_q));  // open: clr
  Register #(.width(32)) x24 (
    .D(multiplexer_32_out), .en(demultiplexer_7_out24), .clk(not_14_out), .Q(x24_q));  // open: clr
  Register #(.width(32)) x23 (
    .D(multiplexer_32_out), .en(demultiplexer_7_out23), .clk(not_14_out), .Q(x23_q));  // open: clr
  Register #(.width(32)) x22 (
    .D(multiplexer_32_out), .en(demultiplexer_7_out22), .clk(not_14_out), .Q(x22_q));  // open: clr
  Register #(.width(32)) x21 (
    .D(multiplexer_32_out), .en(demultiplexer_7_out21), .clk(not_14_out), .Q(x21_q));  // open: clr
  Register #(.width(32)) x20 (
    .D(multiplexer_32_out), .en(demultiplexer_7_out20), .clk(not_14_out), .Q(x20_q));  // open: clr
  Register #(.width(32)) x19 (
    .D(multiplexer_32_out), .en(demultiplexer_7_out19), .clk(not_14_out), .Q(x19_q));  // open: clr
  Register #(.width(32)) x18 (
    .D(multiplexer_32_out), .en(demultiplexer_7_out18), .clk(not_14_out), .Q(x18_q));  // open: clr
  Register #(.width(32)) x17 (
    .D(multiplexer_32_out), .en(demultiplexer_7_out17), .clk(not_14_out), .Q(x17_q));  // open: clr
  Register #(.width(32)) x16 (
    .D(multiplexer_32_out), .en(demultiplexer_7_out16), .clk(not_14_out), .Q(x16_q));  // open: clr
  Register #(.width(32)) x15 (
    .D(multiplexer_32_out), .en(demultiplexer_7_out15), .clk(not_14_out), .Q(x15_q));  // open: clr
  Register #(.width(32)) x14 (
    .D(multiplexer_32_out), .en(demultiplexer_7_out14), .clk(not_14_out), .Q(x14_q));  // open: clr
  Register #(.width(32)) x13 (
    .D(multiplexer_32_out), .en(demultiplexer_7_out13), .clk(not_14_out), .Q(x13_q));  // open: clr
  Register #(.width(32)) x12 (
    .D(multiplexer_32_out), .en(demultiplexer_7_out12), .clk(not_14_out), .Q(x12_q));  // open: clr
  Register #(.width(32)) x11 (
    .D(multiplexer_32_out), .en(demultiplexer_7_out11), .clk(not_14_out), .Q(x11_q));  // open: clr
  Register #(.width(32)) x10 (
    .D(multiplexer_32_out), .en(demultiplexer_7_out10), .clk(not_14_out), .Q(x10_q));  // open: clr
  Register #(.width(32)) x9 (
    .D(multiplexer_32_out), .en(demultiplexer_7_out9), .clk(not_14_out), .Q(x9_q));  // open: clr
  Register #(.width(32)) x8 (
    .D(multiplexer_32_out), .en(demultiplexer_7_out8), .clk(not_14_out), .Q(x8_q));  // open: clr
  Register #(.width(32)) x7 (
    .D(multiplexer_32_out), .en(demultiplexer_7_out7), .clk(not_14_out), .Q(x7_q));  // open: clr
  Register #(.width(32)) x6 (
    .D(multiplexer_32_out), .en(demultiplexer_7_out6), .clk(not_14_out), .Q(x6_q));  // open: clr
  Register #(.width(32)) x5 (
    .D(multiplexer_32_out), .en(demultiplexer_7_out5), .clk(not_14_out), .Q(x5_q));  // open: clr
  Register #(.width(32)) x4 (
    .D(multiplexer_32_out), .en(demultiplexer_7_out4), .clk(not_14_out), .Q(x4_q));  // open: clr
  Register #(.width(32)) x3 (
    .D(multiplexer_32_out), .en(demultiplexer_7_out3), .clk(not_14_out), .Q(x3_q));  // open: clr
  Register #(.width(32)) x2 (
    .D(multiplexer_32_out), .en(demultiplexer_7_out2), .clk(not_14_out), .Q(x2_q));  // open: clr
  Register #(.width(32)) x1 (
    .D(multiplexer_32_out), .en(demultiplexer_7_out1), .clk(not_14_out), .Q(x1_q));  // open: clr
  not not_15 (not_15_out, auipc);
  Multiplexer #(.select(5), .width(32)) multiplexer_34 (
    .in0({32{1'b0}}), .in1(x1_q), .in2(x2_q), .in3(x3_q), .in4(x4_q), .in5(x5_q), .in6(x6_q), .in7(x7_q),
    .in8(x8_q), .in9(x9_q), .in10(x10_q), .in11(x11_q), .in12(x12_q), .in13(x13_q), .in14(x14_q),
    .in15(x15_q), .in16(x16_q), .in17(x17_q), .in18(x18_q), .in19(x19_q), .in20(x20_q), .in21(x21_q),
    .in22(x22_q), .in23(x23_q), .in24(x24_q), .in25(x25_q), .in26(x26_q), .in27(x27_q), .in28(x28_q),
    .in29(x29_q), .in30(x30_q), .in31(x31_q), .out(multiplexer_34_out), .sel(rs1));
  assign reg1 = not_15_out ? multiplexer_34_out : 32'bz;  // Controlled_Buffer controlled_buffer_25
  Multiplexer #(.select(5), .width(32)) multiplexer_35 (
    .in0({32{1'b0}}), .in1(x1_q), .in2(x2_q), .in3(x3_q), .in4(x4_q), .in5(x5_q), .in6(x6_q), .in7(x7_q),
    .in8(x8_q), .in9(x9_q), .in10(x10_q), .in11(x11_q), .in12(x12_q), .in13(x13_q), .in14(x14_q),
    .in15(x15_q), .in16(x16_q), .in17(x17_q), .in18(x18_q), .in19(x19_q), .in20(x20_q), .in21(x21_q),
    .in22(x22_q), .in23(x23_q), .in24(x24_q), .in25(x25_q), .in26(x26_q), .in27(x27_q), .in28(x28_q),
    .in29(x29_q), .in30(x30_q), .in31(x31_q), .out(reg2), .sel(rs2));

  // Notes on the sheet:
  //   ValGen Unit
  //   contents of rom_1 (hex, n*v repeats v):
  //   7 0 0 0 83 303 0 0 10a 0 0 0 41 303 10*0 2d0 23 0 421 1
  //   PC
  //   Decoder
  //   SysControl Unit
  //   ImmGen Unit
  //   MMIO
  //   contents of rom_2 (hex, n*v repeats v):
  //   0 5 c d 4 6 3 2 8*0 1 4*0 7
  //   contents of rom_3 (hex, n*v repeats v):
  //   8 9 0 0 c a d b
  //   ACU
  //   CSRF
  //   RAM
  //   ALU
  //   CSR Logic Unit
  //   RegFile
endmodule
